# Fritzing sketch mario_clock (saved by Fritzing 0.9.3b)
breadboards: 1

parts:
  Part1 = Espruino Pico  # not connected
  INK1 = Nokia 5110 INK Display [part_number="Nokia 5110"]  # not connected
  J1 = Piezo Speaker  # not connected
  S1 = Momentary Switch [package=ksa_sealed_tac_switch]
  S2 = Momentary Switch [package=ksa_sealed_tac_switch]

nets:
  N1: S1.1, S1.2
  N2: S1.3, S1.4, S2.3, S2.4
  N3: S2.1, S2.2

custom parts:
  Nokia 5110 INK Display: Nokia 5110 INK display - with Bottom Row Pin Connections. Note: these devices are typically 3.3V only and need a level translator such as the 74ahc367 (whose inputs are 5V tolerant when VCC is 3.3V) to operate from a 5V device such as an Arduino.
